// Logisim project AOC 16 Tarefa - Transmissão Serial de Bits - Henrique Furtado.circ as structural Verilog: 2 circuits, main circuit main
module main (
  input  Sincronia,
  input  Entrada,
  input  in_3,
  input  in_4,
  input  in_5
);

  wire and_1_out, and_2_out, and_3_out, and_4_out, clock_1_out, d_ff_1_q, d_ff_2_q, d_ff_3_q, d_ff_4_q,
       d_ff_5_q, d_ff_6_q, d_ff_7_q, d_ff_8_q, d_ff_9_q, d_ff_10_q, d_ff_11_q, d_ff_12_q, d_ff_13_q,
       d_ff_14_q, d_ff_15_q, d_ff_16_q, led_1_a2, led_1_b2, led_1_c2, led_1_d2, led_1_e, led_1_f, led_1_g,
       led_2_a2, led_2_b2, led_2_c2, led_2_d2, led_2_e, led_2_f, led_2_g, or_1_out;

  Clock clock_1 (.out(clock_1_out));
  D_Flip_Flop d_ff_1 (.clk(clock_1_out), .D(d_ff_4_q), .Q(d_ff_1_q), .preset(Sincronia));  // open: Qn, en, reset
  LED led_1 (
    .a(Entrada), .b(in_3), .c(in_4), .d(in_5), .a2(led_1_a2), .b2(led_1_b2), .c2(led_1_c2), .d2(led_1_d2),
    .e(led_1_e), .f(led_1_f), .g(led_1_g));
  _7_Segment_Display u_7_segment_display_1 (
    .g(led_1_g), .f(led_1_f), .a(led_1_a2), .b(led_1_b2), .e(led_1_e), .d(led_1_d2), .c(led_1_c2));  // open: dp
  D_Flip_Flop d_ff_2 (.clk(clock_1_out), .D(d_ff_1_q), .Q(d_ff_2_q), .reset(Sincronia));  // open: Qn, preset, en
  D_Flip_Flop d_ff_3 (.clk(clock_1_out), .D(d_ff_2_q), .Q(d_ff_3_q), .reset(Sincronia));  // open: Qn, preset, en
  D_Flip_Flop d_ff_4 (.clk(clock_1_out), .D(d_ff_3_q), .Q(d_ff_4_q), .reset(Sincronia));  // open: Qn, preset, en
  and and_1 (and_1_out, d_ff_1_q, Entrada);
  and and_2 (and_2_out, d_ff_2_q, in_3);
  and and_3 (and_3_out, d_ff_3_q, in_4);
  and and_4 (and_4_out, d_ff_4_q, in_5);
  or or_1 (or_1_out, and_1_out, and_2_out, and_3_out, and_4_out);
  D_Flip_Flop d_ff_5 (.clk(clock_1_out), .D(or_1_out), .Q(d_ff_5_q));  // open: Qn, preset, en, reset
  D_Flip_Flop d_ff_6 (.clk(clock_1_out), .D(d_ff_15_q), .Q(d_ff_6_q), .preset(Sincronia));  // open: Qn, en, reset
  D_Flip_Flop d_ff_7 (.clk(clock_1_out), .D(d_ff_5_q), .Q(d_ff_7_q));  // open: Qn, preset, en, reset
  D_Flip_Flop d_ff_8 (.clk(d_ff_6_q), .D(d_ff_5_q), .Q(d_ff_8_q));  // open: Qn, preset, en, reset
  D_Flip_Flop d_ff_9 (.clk(clock_1_out), .D(d_ff_6_q), .Q(d_ff_9_q), .reset(Sincronia));  // open: Qn, preset, en
  D_Flip_Flop d_ff_10 (.clk(clock_1_out), .D(d_ff_7_q), .Q(d_ff_10_q));  // open: Qn, preset, en, reset
  D_Flip_Flop d_ff_11 (.clk(d_ff_6_q), .D(d_ff_7_q), .Q(d_ff_11_q));  // open: Qn, preset, en, reset
  LED led_2 (
    .a(d_ff_16_q), .b(d_ff_14_q), .c(d_ff_11_q), .d(d_ff_8_q), .a2(led_2_a2), .b2(led_2_b2), .c2(led_2_c2),
    .d2(led_2_d2), .e(led_2_e), .f(led_2_f), .g(led_2_g));
  _7_Segment_Display u_7_segment_display_2 (
    .g(led_2_g), .f(led_2_f), .a(led_2_a2), .b(led_2_b2), .e(led_2_e), .d(led_2_d2), .c(led_2_c2));  // open: dp
  D_Flip_Flop d_ff_12 (.clk(clock_1_out), .D(d_ff_9_q), .Q(d_ff_12_q), .reset(Sincronia));  // open: Qn, preset, en
  D_Flip_Flop d_ff_13 (.clk(clock_1_out), .D(d_ff_10_q), .Q(d_ff_13_q));  // open: Qn, preset, en, reset
  D_Flip_Flop d_ff_14 (.clk(d_ff_6_q), .D(d_ff_10_q), .Q(d_ff_14_q));  // open: Qn, preset, en, reset
  D_Flip_Flop d_ff_15 (.clk(clock_1_out), .D(d_ff_12_q), .Q(d_ff_15_q), .reset(Sincronia));  // open: Qn, preset, en
  D_Flip_Flop d_ff_16 (.clk(d_ff_6_q), .D(d_ff_13_q), .Q(d_ff_16_q));  // open: Qn, preset, en, reset

  // Notes on the sheet:
  //   Clock
  //   Local A
  //   Informação a ser transmitida
  //   Contador
  //   Cabo de Transimssão
  //   Buffer do display
  //   Local B
  //   Registrador deslocamento
  //   Informação recebida
  //   Contador
endmodule

module LED (
  input  a,
  input  b,
  input  c,
  input  d,
  output a2,
  output b2,
  output c2,
  output d2,
  output e,
  output f,
  output g
);

  wire and_1_out, and_2_out, and_3_out, and_4_out, and_5_out, and_6_out, and_7_out, and_8_out, and_9_out,
       and_10_out, and_11_out, and_12_out, and_13_out, and_14_out, and_15_out, and_16_out, and_17_out,
       and_18_out, and_19_out, and_20_out, and_21_out, and_22_out, and_23_out, and_24_out, and_25_out,
       and_26_out, and_27_out, and_28_out, and_29_out, and_30_out, and_31_out, and_32_out, and_33_out,
       and_34_out, and_35_out, not_1_out, not_2_out, not_3_out, not_4_out, not_5_out, not_6_out, not_7_out,
       not_8_out, not_9_out, not_10_out, not_11_out, not_12_out, not_13_out, not_14_out, not_15_out,
       not_16_out, not_17_out, not_18_out, not_19_out, not_20_out, not_21_out, not_22_out, not_23_out,
       not_24_out, not_25_out, not_26_out, not_27_out, not_28_out, not_29_out, not_30_out, not_31_out,
       not_32_out, not_33_out, not_34_out, not_35_out, not_36_out, not_37_out, not_38_out, not_39_out,
       not_40_out, not_41_out, not_42_out, not_43_out;

  not not_1 (not_1_out, b);
  and and_1 (and_1_out, not_1_out, not_2_out);
  not not_2 (not_2_out, d);
  not not_3 (not_3_out, a);
  and and_2 (and_2_out, not_3_out, c);
  not not_4 (not_4_out, a);
  and and_3 (and_3_out, not_4_out, b, d);
  and and_4 (and_4_out, b, c);
  not not_5 (not_5_out, b);
  and and_5 (and_5_out, a, not_5_out, not_6_out);
  not not_6 (not_6_out, c);
  and and_6 (and_6_out, a, not_7_out);
  not not_7 (not_7_out, d);
  not not_8 (not_8_out, a);
  and and_7 (and_7_out, not_8_out, not_9_out);
  not not_9 (not_9_out, b);
  not not_10 (not_10_out, a);
  not not_11 (not_11_out, c);
  and and_8 (and_8_out, not_10_out, not_11_out, not_12_out);
  not not_12 (not_12_out, d);
  not not_13 (not_13_out, b);
  and and_9 (and_9_out, not_13_out, not_14_out);
  not not_14 (not_14_out, d);
  not not_15 (not_15_out, a);
  and and_10 (and_10_out, not_15_out, c, d);
  not not_16 (not_16_out, c);
  and and_11 (and_11_out, a, not_16_out, d);
  not not_17 (not_17_out, a);
  and and_12 (and_12_out, not_17_out, not_18_out);
  not not_18 (not_18_out, c);
  not not_19 (not_19_out, a);
  and and_13 (and_13_out, not_19_out, d);
  not not_20 (not_20_out, c);
  and and_14 (and_14_out, not_20_out, d);
  not not_21 (not_21_out, a);
  and and_15 (and_15_out, not_21_out, b);
  and and_16 (and_16_out, a, not_22_out);
  not not_22 (not_22_out, b);
  not not_23 (not_23_out, a);
  not not_24 (not_24_out, b);
  and and_17 (and_17_out, not_23_out, not_24_out, not_25_out);
  not not_25 (not_25_out, d);
  not not_26 (not_26_out, b);
  and and_18 (and_18_out, not_26_out, c, d);
  not not_27 (not_27_out, c);
  and and_19 (and_19_out, b, not_27_out, d);
  and and_20 (and_20_out, b, c, not_28_out);
  not not_28 (not_28_out, d);
  and and_21 (and_21_out, a, not_29_out);
  not not_29 (not_29_out, c);
  not not_30 (not_30_out, b);
  and and_22 (and_22_out, not_30_out, not_31_out);
  not not_31 (not_31_out, d);
  and and_23 (and_23_out, c, not_32_out);
  not not_32 (not_32_out, d);
  and and_24 (and_24_out, a, c);
  and and_25 (and_25_out, a, b);
  not not_33 (not_33_out, c);
  and and_26 (and_26_out, not_33_out, not_34_out);
  not not_34 (not_34_out, d);
  not not_35 (not_35_out, a);
  and and_27 (and_27_out, not_35_out, b, not_36_out);
  not not_36 (not_36_out, c);
  and and_28 (and_28_out, b, not_37_out);
  not not_37 (not_37_out, d);
  and and_29 (and_29_out, a, not_38_out);
  not not_38 (not_38_out, b);
  and and_30 (and_30_out, a, c);
  not not_39 (not_39_out, b);
  and and_31 (and_31_out, not_39_out, c);
  and and_32 (and_32_out, c, not_40_out);
  not not_40 (not_40_out, d);
  not not_41 (not_41_out, a);
  and and_33 (and_33_out, not_41_out, b, not_42_out);
  not not_42 (not_42_out, c);
  and and_34 (and_34_out, a, not_43_out);
  not not_43 (not_43_out, b);
  and and_35 (and_35_out, a, d);
  or or_1 (b2, and_7_out, and_8_out, and_9_out, and_10_out, and_11_out);
  or or_2 (c2, and_12_out, and_13_out, and_14_out, and_15_out, and_16_out);
  or or_3 (d2, and_17_out, and_18_out, and_19_out, and_20_out, and_21_out);
  or or_4 (e, and_22_out, and_23_out, and_24_out, and_25_out);
  or or_5 (f, and_26_out, and_27_out, and_28_out, and_29_out, and_30_out);
  or or_6 (g, and_31_out, and_32_out, and_33_out, and_34_out, and_35_out);
  or or_7 (a2, and_1_out, and_2_out, and_3_out, and_4_out, and_5_out, and_6_out);
endmodule
