// Logisim project Calculadora Henrique Furtado.circ as structural Verilog: 5 circuits, main circuit main
module main (
  input  in_1,
  input  Modo,
  input  \Número_A ,
  input  in_4,
  input  in_5,
  input  \Número_B 
);

  wire and_1_out, and_2_out, and_3_out, and_4_out, and_5_out, and_6_out, and_7_out, and_8_out, and_9_out,
       and_10_out, and_11_out, and_12_out, and_13_out, and_14_out, and_15_out, led_1_a2, led_1_b2, led_1_c2,
       led_1_d2, led_1_e, led_1_f, led_1_g, led_2_a2, led_2_b2, led_2_c2, led_2_d2, led_2_e, led_2_f,
       led_2_g, led_3_a2, led_3_b2, led_3_c2, led_3_d2, led_3_e, led_3_f, led_3_g, \multiplicação_1_s1 ,
       \multiplicação_1_s2 , \multiplicação_1_s3 , \multiplicação_1_s4 , or_1_out, or_2_out, or_3_out,
       or_4_out, soma_1_s1, soma_1_s2, soma_1_s3, soma_1_s4, \subtração_1_negativo , \subtração_1_s1 ,
       \subtração_1_s2 , \subtração_1_s3 , \subtração_1_s4 ;

  LED led_1 (
    .a(1'b0), .b(1'b0), .c(\Número_A ), .d(in_4), .a2(led_1_a2), .b2(led_1_b2), .c2(led_1_c2), .d2(led_1_d2),
    .e(led_1_e), .f(led_1_f), .g(led_1_g));
  _7_Segment_Display u_7_segment_display_1 (
    .g(led_1_g), .f(led_1_f), .a(led_1_a2), .b(led_1_b2), .e(led_1_e), .d(led_1_d2), .c(led_1_c2));  // open: dp
  and and_1 (and_1_out, in_4, and_3_out);
  and and_2 (and_2_out, \Número_A , and_3_out);
  SOMA soma_1 (
    .a1(and_4_out), .a2(and_5_out), .b1(and_2_out), .b2(and_1_out), .s1(soma_1_s1), .s2(soma_1_s2),
    .s3(soma_1_s3), .s4(soma_1_s4));
  _7_Segment_Display u_7_segment_display_2 (
    .g(led_2_g), .f(led_2_f), .a(led_2_a2), .b(led_2_b2), .e(led_2_e), .d(led_2_d2), .c(led_2_c2));  // open: dp
  and and_3 (and_3_out, ~Modo, in_1);  // AND_Gate
  and and_4 (and_4_out, \Número_B , and_3_out);
  and and_5 (and_5_out, in_5, and_3_out);
  LED led_2 (
    .a(1'b0), .b(1'b0), .c(\Número_B ), .d(in_5), .a2(led_2_a2), .b2(led_2_b2), .c2(led_2_c2), .d2(led_2_d2),
    .e(led_2_e), .f(led_2_f), .g(led_2_g));
  or or_1 (or_1_out, soma_1_s4, \subtração_1_s4 , \multiplicação_1_s4 );
  or or_2 (or_2_out, soma_1_s3, \subtração_1_s3 , \multiplicação_1_s3 );
  and and_6 (and_6_out, Modo, ~in_1);  // AND_Gate
  or or_3 (or_3_out, soma_1_s1, \subtração_1_s1 , \multiplicação_1_s1 );
  or or_4 (or_4_out, soma_1_s2, \subtração_1_s2 , \multiplicação_1_s2 );
  and and_7 (and_7_out, \Número_A , and_6_out);
  and and_8 (and_8_out, in_4, and_6_out);
  \MULTIPLICAÇÃO  \multiplicação_1  (
    .a1(and_9_out), .a2(and_10_out), .b1(and_7_out), .b2(and_8_out), .s1(\multiplicação_1_s1 ),
    .s2(\multiplicação_1_s2 ), .s3(\multiplicação_1_s3 ), .s4(\multiplicação_1_s4 ));
  _7_Segment_Display u_7_segment_display_3 (
    .g(led_3_g), .f(led_3_f), .a(led_3_a2), .b(led_3_b2), .e(led_3_e), .d(led_3_d2), .c(led_3_c2),
    .dp(\subtração_1_negativo ));
  and and_9 (and_9_out, \Número_B , and_6_out);
  and and_10 (and_10_out, in_5, and_6_out);
  LED led_3 (
    .a(or_3_out), .b(or_4_out), .c(or_2_out), .d(or_1_out), .a2(led_3_a2), .b2(led_3_b2), .c2(led_3_c2),
    .d2(led_3_d2), .e(led_3_e), .f(led_3_f), .g(led_3_g));
  and and_11 (and_11_out, in_1, Modo);
  and and_12 (and_12_out, \Número_B , and_11_out);
  and and_13 (and_13_out, in_5, and_11_out);
  and and_14 (and_14_out, in_4, and_11_out);
  and and_15 (and_15_out, \Número_A , and_11_out);
  \SUBTRAÇÃO  \subtração_1  (
    .a1(and_15_out), .a2(and_14_out), .b1(and_12_out), .b2(and_13_out), .s1(\subtração_1_s1 ),
    .s2(\subtração_1_s2 ), .s3(\subtração_1_s3 ), .s4(\subtração_1_s4 ), .negativo(\subtração_1_negativo ));

  // Notes on the sheet:
  //   1 0 - Adição
  //   0 1 - Mulitplicação
  //   1 1 - Subtração
  //   Entrada de Dados
  //   Número A
  //   Visualização de Dados
  //   Soma
  //   Número B
  //   Multiplicação
  //   Resultado
  //   Ponto = Negativo
  //   Subtração
endmodule

module SOMA (
  input  a1,
  input  a2,
  input  b1,
  input  b2,
  output s1,
  output s2,
  output s3,
  output s4
);

  wire and_1_out, and_2_out, and_3_out, and_4_out, and_5_out, and_6_out, and_7_out, and_8_out, and_9_out,
       and_10_out, and_11_out, not_1_out, not_2_out, not_3_out, not_4_out, not_5_out, not_6_out, not_7_out,
       not_8_out, not_9_out, not_10_out, not_11_out, not_12_out;

  and and_1 (and_1_out, a2, b1, b2);
  and and_2 (and_2_out, a1, b1);
  and and_3 (and_3_out, a1, a2, b2);
  not not_1 (not_1_out, a1);
  not not_2 (not_2_out, a2);
  not not_3 (not_3_out, a1);
  not not_4 (not_4_out, b2);
  not not_5 (not_5_out, a1);
  not not_6 (not_6_out, b1);
  not not_7 (not_7_out, a2);
  not not_8 (not_8_out, b1);
  not not_9 (not_9_out, b1);
  not not_10 (not_10_out, b2);
  not not_11 (not_11_out, a2);
  and and_4 (and_4_out, not_11_out, b2);
  and and_5 (and_5_out, a2, not_12_out);
  not not_12 (not_12_out, b2);
  or or_1 (s2, and_1_out, and_2_out, and_3_out);
  and and_6 (and_6_out, not_1_out, not_2_out, b1);
  and and_7 (and_7_out, not_3_out, b1, not_4_out);
  and and_8 (and_8_out, not_5_out, a2, not_6_out, b2);
  and and_9 (and_9_out, a1, not_7_out, not_8_out);
  and and_10 (and_10_out, a1, not_9_out, not_10_out);
  and and_11 (and_11_out, a1, a2, b1, b2);
  or or_2 (s4, and_4_out, and_5_out);
  or or_3 (s3, and_6_out, and_7_out, and_8_out, and_9_out, and_10_out, and_11_out);

  assign s1 = 1'b0;
endmodule

module LED (
  input  a,
  input  b,
  input  c,
  input  d,
  output a2,
  output b2,
  output c2,
  output d2,
  output e,
  output f,
  output g
);

  wire and_1_out, and_2_out, and_3_out, and_4_out, and_5_out, and_6_out, and_7_out, and_8_out, and_9_out,
       and_10_out, and_11_out, and_12_out, and_13_out, and_14_out, and_15_out, and_16_out, and_17_out,
       and_18_out, and_19_out, and_20_out, and_21_out, and_22_out, and_23_out, and_24_out, and_25_out,
       and_26_out, and_27_out, and_28_out, and_29_out, and_30_out, and_31_out, and_32_out, and_33_out,
       and_34_out, and_35_out, not_1_out, not_2_out, not_3_out, not_4_out, not_5_out, not_6_out, not_7_out,
       not_8_out, not_9_out, not_10_out, not_11_out, not_12_out, not_13_out, not_14_out, not_15_out,
       not_16_out, not_17_out, not_18_out, not_19_out, not_20_out, not_21_out, not_22_out, not_23_out,
       not_24_out, not_25_out, not_26_out, not_27_out, not_28_out, not_29_out, not_30_out, not_31_out,
       not_32_out, not_33_out, not_34_out, not_35_out, not_36_out, not_37_out, not_38_out, not_39_out,
       not_40_out, not_41_out, not_42_out, not_43_out;

  not not_1 (not_1_out, b);
  and and_1 (and_1_out, not_1_out, not_2_out);
  not not_2 (not_2_out, d);
  not not_3 (not_3_out, a);
  and and_2 (and_2_out, not_3_out, c);
  not not_4 (not_4_out, a);
  and and_3 (and_3_out, not_4_out, b, d);
  and and_4 (and_4_out, b, c);
  not not_5 (not_5_out, b);
  and and_5 (and_5_out, a, not_5_out, not_6_out);
  not not_6 (not_6_out, c);
  and and_6 (and_6_out, a, not_7_out);
  not not_7 (not_7_out, d);
  not not_8 (not_8_out, a);
  and and_7 (and_7_out, not_8_out, not_9_out);
  not not_9 (not_9_out, b);
  not not_10 (not_10_out, a);
  not not_11 (not_11_out, c);
  and and_8 (and_8_out, not_10_out, not_11_out, not_12_out);
  not not_12 (not_12_out, d);
  not not_13 (not_13_out, b);
  and and_9 (and_9_out, not_13_out, not_14_out);
  not not_14 (not_14_out, d);
  not not_15 (not_15_out, a);
  and and_10 (and_10_out, not_15_out, c, d);
  not not_16 (not_16_out, c);
  and and_11 (and_11_out, a, not_16_out, d);
  not not_17 (not_17_out, a);
  and and_12 (and_12_out, not_17_out, not_18_out);
  not not_18 (not_18_out, c);
  not not_19 (not_19_out, a);
  and and_13 (and_13_out, not_19_out, d);
  not not_20 (not_20_out, c);
  and and_14 (and_14_out, not_20_out, d);
  not not_21 (not_21_out, a);
  and and_15 (and_15_out, not_21_out, b);
  and and_16 (and_16_out, a, not_22_out);
  not not_22 (not_22_out, b);
  not not_23 (not_23_out, a);
  not not_24 (not_24_out, b);
  and and_17 (and_17_out, not_23_out, not_24_out, not_25_out);
  not not_25 (not_25_out, d);
  not not_26 (not_26_out, b);
  and and_18 (and_18_out, not_26_out, c, d);
  and and_19 (and_19_out, b, not_27_out, d);
  not not_27 (not_27_out, c);
  and and_20 (and_20_out, b, c, not_28_out);
  not not_28 (not_28_out, d);
  and and_21 (and_21_out, a, not_29_out);
  not not_29 (not_29_out, c);
  not not_30 (not_30_out, b);
  and and_22 (and_22_out, not_30_out, not_31_out);
  not not_31 (not_31_out, d);
  and and_23 (and_23_out, c, not_32_out);
  not not_32 (not_32_out, d);
  and and_24 (and_24_out, a, c);
  and and_25 (and_25_out, a, b);
  not not_33 (not_33_out, c);
  and and_26 (and_26_out, not_33_out, not_34_out);
  not not_34 (not_34_out, d);
  not not_35 (not_35_out, a);
  and and_27 (and_27_out, not_35_out, b, not_36_out);
  not not_36 (not_36_out, c);
  and and_28 (and_28_out, b, not_37_out);
  not not_37 (not_37_out, d);
  and and_29 (and_29_out, a, not_38_out);
  not not_38 (not_38_out, b);
  and and_30 (and_30_out, a, c);
  not not_39 (not_39_out, b);
  and and_31 (and_31_out, not_39_out, c);
  and and_32 (and_32_out, c, not_40_out);
  not not_40 (not_40_out, d);
  not not_41 (not_41_out, a);
  and and_33 (and_33_out, not_41_out, b, not_42_out);
  not not_42 (not_42_out, c);
  and and_34 (and_34_out, a, not_43_out);
  not not_43 (not_43_out, b);
  and and_35 (and_35_out, a, d);
  or or_1 (b2, and_7_out, and_8_out, and_9_out, and_10_out, and_11_out);
  or or_2 (c2, and_12_out, and_13_out, and_14_out, and_15_out, and_16_out);
  or or_3 (d2, and_17_out, and_18_out, and_19_out, and_20_out, and_21_out);
  or or_4 (e, and_22_out, and_23_out, and_24_out, and_25_out);
  or or_5 (f, and_26_out, and_27_out, and_28_out, and_29_out, and_30_out);
  or or_6 (g, and_31_out, and_32_out, and_33_out, and_34_out, and_35_out);
  or or_7 (a2, and_1_out, and_2_out, and_3_out, and_4_out, and_5_out, and_6_out);
endmodule

module \MULTIPLICAÇÃO  (
  input  a1,
  input  a2,
  input  b1,
  input  b2,
  output s1,
  output s2,
  output s3,
  output s4
);

  wire and_2_out, and_3_out, and_4_out, and_5_out, and_6_out, and_7_out, not_1_out, not_2_out, not_3_out,
       not_4_out, not_5_out, not_6_out;

  and and_1 (s1, a1, a2, b1, b2);
  and and_2 (and_2_out, a1, not_1_out, b1);
  not not_1 (not_1_out, a2);
  and and_3 (and_3_out, a1, b1, not_2_out);
  not not_2 (not_2_out, b2);
  not not_3 (not_3_out, a1);
  and and_4 (and_4_out, not_3_out, a2, b1);
  and and_5 (and_5_out, a2, b1, not_4_out);
  not not_4 (not_4_out, b2);
  and and_6 (and_6_out, a1, not_5_out, b2);
  not not_5 (not_5_out, a2);
  and and_7 (and_7_out, a1, not_6_out, b2);
  not not_6 (not_6_out, b1);
  and and_8 (s4, a2, b2);
  or or_1 (s2, and_2_out, and_3_out);
  or or_2 (s3, and_4_out, and_5_out, and_6_out, and_7_out);
endmodule

module \SUBTRAÇÃO  (
  input  a1,
  input  a2,
  input  b1,
  input  b2,
  output s1,
  output s2,
  output s3,
  output s4,
  output negativo
);

  wire and_1_out, and_2_out, and_3_out, and_4_out, and_5_out, and_6_out, and_7_out, and_8_out, and_9_out,
       not_1_out, not_2_out, not_3_out, not_4_out, not_5_out, not_6_out, not_7_out, not_8_out, not_9_out,
       not_10_out, not_11_out, not_12_out;

  not not_1 (not_1_out, a1);
  not not_2 (not_2_out, a2);
  and and_1 (and_1_out, not_1_out, not_2_out, b1);
  not not_3 (not_3_out, a1);
  and and_2 (and_2_out, not_3_out, b1, b2);
  not not_4 (not_4_out, b1);
  and and_3 (and_3_out, a1, not_4_out, not_5_out);
  not not_5 (not_5_out, b2);
  and and_4 (and_4_out, a1, a2, not_6_out);
  not not_6 (not_6_out, b1);
  not not_7 (not_7_out, a2);
  and and_5 (and_5_out, not_7_out, b2);
  and and_6 (and_6_out, a2, not_8_out);
  not not_8 (not_8_out, b2);
  not not_9 (not_9_out, a1);
  not not_10 (not_10_out, a2);
  and and_7 (and_7_out, not_9_out, not_10_out, b2);
  not not_11 (not_11_out, a1);
  and and_8 (and_8_out, not_11_out, b1);
  not not_12 (not_12_out, a2);
  and and_9 (and_9_out, not_12_out, b1, b2);
  or or_1 (s3, and_1_out, and_2_out, and_3_out, and_4_out);
  or or_2 (s4, and_5_out, and_6_out);
  or or_3 (negativo, and_7_out, and_8_out, and_9_out);

  assign s1 = 1'b0;
  assign s2 = 1'b0;
endmodule
